# Fritzing sketch geigerSimulator (saved by Fritzing 0.9.3b)
breadboards: 1

parts:
  KY-1 = Keyes Relay [package=THT]
  Part1 = Arduino Uno (Rev3) - ICSP
  hc-sr1 = hc-sr04

nets:
  N1: KY-1.signal, Part1.D8
  5V: KY-1.power, Part1.5V, hc-sr1.VCC
  GND: KY-1.ground, Part1.GND, hc-sr1.GND
  N2: Part1.D2, hc-sr1.Echo
  N3: Part1.D3_PWM, hc-sr1.Trig

custom parts:
  Keyes Relay: The Keyes 5V relay module is suitable for SCM development, home appliance control. It uses a 5V~12V TIL control signal which can control DC / AC signal.
